// Logisim project cpu.circ as structural Verilog: 1 circuit, main circuit cpu
module cpu (
  input  clk,
  input  [31:0] Instruction,
  input  [31:0] MemReadData,
  output [31:0] MemAddress,
  output [31:0] ProgramCounter,
  output [31:0] ra,
  output [31:0] sp,
  output [31:0] t0,
  output [31:0] t1,
  output [31:0] t2,
  output [31:0] s0,
  output [31:0] s1,
  output [31:0] a0,
  output [3:0] MemWriteMask,
  output [31:0] MemWriteData
);

  wire ASel, BrEq, BrLt, BrUn, BSel, MemWEn, PCSel, RegWEn;
  wire [1:0] alu_out, WBSel;
  wire [2:0] Immsel;
  wire [3:0] ALUSel;
  wire [31:0] adder_1_out, adder_2_out, DataToReg, imm_out, Instruction2, multiplexer_1_out,
       multiplexer_4_out, multiplexer_5_out, ProgramCounter2, rs1_out, rs2_out, wb;
  wire [63:0] multiplexer_2_out;

  Adder #(.width(32)) adder_1 (.a(ProgramCounter), .b(32'h4), .out(adder_1_out));  // open: cin, cout
  Multiplexer #(.width(32)) multiplexer_1 (
    .in0(adder_1_out), .in1({MemAddress[31:2], alu_out}), .out(multiplexer_1_out), .sel(PCSel));
  Register #(.width(32)) PC (.D(multiplexer_1_out), .clk(clk), .Q(ProgramCounter));  // open: en, clr
  Register #(.width(64)) register_1 (
    .D(multiplexer_2_out), .en(1'b1), .clk(clk), .Q({Instruction2, ProgramCounter2}));  // open: clr
  Multiplexer #(.width(64)) multiplexer_2 (
    .in0({Instruction, ProgramCounter}), .in1(64'h33), .out(multiplexer_2_out), .sel(PCSel));
  Adder #(.width(32)) adder_2 (.a(ProgramCounter2), .b(32'h4), .out(adder_2_out));  // open: cin, cout
  Multiplexer #(.select(2), .width(32)) multiplexer_3 (
    .in0(DataToReg), .in1({MemAddress[31:2], alu_out}), .in2(adder_2_out), .out(wb), .sel(WBSel));  // open: in3
  control_logic control_logic_1 (
    .Instruction(Instruction2), .BrEq(BrEq), .BrLt(BrLt), .PCSel(PCSel), .RegWEn(RegWEn), .ImmSel(Immsel),
    .BrUn(BrUn), .ASel(ASel), .BSel(BSel), .ALUSel(ALUSel), .MemWEn(MemWEn), .WBSel(WBSel));
  regfile regfile_1 (
    .ReadIndex1(Instruction2[19:15]), .ReadIndex2(Instruction2[24:20]), .WriteIndex(Instruction2[11:7]),
    .WriteData(wb), .RegWEn(RegWEn), .clk(clk), .ra(ra), .sp(sp), .t0(t0), .t1(t1), .t2(t2), .s0(s0),
    .s1(s1), .a0(a0), .ReadData1(rs1_out), .ReadData2(rs2_out));
  imm_gen imm_gen_1 (.Instruction(Instruction2), .ImmSel(Immsel), .Immediate(imm_out));
  Multiplexer #(.width(32)) multiplexer_4 (.in0(rs1_out), .in1(ProgramCounter2), .out(multiplexer_4_out), .sel(ASel));
  Multiplexer #(.width(32)) multiplexer_5 (.in0(rs2_out), .in1(imm_out), .out(multiplexer_5_out), .sel(BSel));
  alu alu_1 (.A(multiplexer_4_out), .B(multiplexer_5_out), .ALUSel(ALUSel), .ALUResult({MemAddress[31:2], alu_out}));
  branch_comp branch_comp_1 (.BrData1(rs1_out), .BrData2(rs2_out), .BrUn(BrUn), .BrEq(BrEq), .BrLt(BrLt));
  partial_store partial_store_1 (
    .Instruction(Instruction2), .MemAddress({MemAddress[31:2], 2'b00}), .DataFromReg(rs2_out),
    .MemWEn(MemWEn), .MemWriteMask(MemWriteMask), .DataToMem(MemWriteData));
  partial_load partial_load_1 (
    .Instruction(Instruction2), .MemAddress({MemAddress[31:2], 2'b00}), .DataFromMem(MemReadData),
    .DataToReg(DataToReg));

  assign MemAddress[1:0] = 2'b00;

  // Other names for the same wires on the sheet: rd[4:0] = Instruction2[11:7]; rs1[4:0] = Instruction2[19:15];
  //   rs2[4:0] = Instruction2[24:20]; alu_out[31:2] = MemAddress[31:2]

  // Notes on the sheet:
  //   To IMEM
  //   IMEM (do **NOT** move this)
  //   From IMEM
  //   Inputs/Outputs for testing. Do **NOT** move these.
  //   It is OK to move the PC, RegFile, ALU, MEM, Branch Comp, Imm Gen, Partial Load, Partial Store and Control Logic to wherever is most convenient for you when constructing your CPU, and to delete this text
  //   To DMEM
  //   DMEM (do **NOT** move this)
  //   From DMEM
endmodule
