// Logisim project partial-store.circ as structural Verilog: 1 circuit, main circuit partial_store
module partial_store (
  input  [31:0] Instruction,
  input  [31:0] MemAddress,
  input  [31:0] DataFromReg,
  input  MemWEn,
  output [3:0] MemWriteMask,
  output [31:0] DataToMem
);

  wire [1:0] demultiplexer_2_out0, demultiplexer_2_out1;
  wire [3:0] demultiplexer_1_out0, multiplexer_1_out;
  wire [7:0] demultiplexer_3_out0, demultiplexer_3_out1, demultiplexer_3_out2, demultiplexer_3_out3;
  wire [15:0] demultiplexer_4_out0, demultiplexer_4_out1;

  Demultiplexer #(.select(2)) demultiplexer_1 (
    .out0(demultiplexer_1_out0[0]), .out1(demultiplexer_1_out0[1]), .out2(demultiplexer_1_out0[2]),
    .out3(demultiplexer_1_out0[3]), .in(1'b1), .sel(MemAddress[1:0]));
  Demultiplexer #(.width(2)) demultiplexer_2 (
    .out0(demultiplexer_2_out0), .out1(demultiplexer_2_out1), .in(2'b11), .sel(MemAddress[1]));
  Multiplexer #(.select(2), .width(4)) multiplexer_1 (
    .in0(demultiplexer_1_out0), .in1({demultiplexer_2_out1, demultiplexer_2_out0}), .in2(4'b1111),
    .out(multiplexer_1_out), .sel(Instruction[13:12]));  // open: in3
  Multiplexer #(.width(4)) multiplexer_2 (.in0(4'b0000), .in1(multiplexer_1_out), .out(MemWriteMask), .sel(MemWEn));
  Demultiplexer #(.select(2), .width(8)) demultiplexer_3 (
    .out0(demultiplexer_3_out0), .out1(demultiplexer_3_out1), .out2(demultiplexer_3_out2),
    .out3(demultiplexer_3_out3), .in(DataFromReg[7:0]), .sel(MemAddress[1:0]));
  Demultiplexer #(.width(16)) demultiplexer_4 (
    .out0(demultiplexer_4_out0), .out1(demultiplexer_4_out1), .in(DataFromReg[15:0]), .sel(MemAddress[1]));
  Multiplexer #(.select(2), .width(32)) multiplexer_3 (
    .in0({demultiplexer_3_out3, demultiplexer_3_out2, demultiplexer_3_out1, demultiplexer_3_out0}),
    .in1({demultiplexer_4_out1, demultiplexer_4_out0}), .in2(DataFromReg), .out(DataToMem),
    .sel(Instruction[13:12]));  // open: in3

  // Other names for the same wires on the sheet: funct3[1:0] = Instruction[13:12]; low2bit[1:0] = MemAddress[1:0]

  // Notes on the sheet:
  //   INPUTS to your circuit
  //   DON'T CHANGE THE LOCATIONS OF THE INPUTS AND OUTPUTS!
  //   OUTPUT from your circuit
endmodule
