// Logisim project regfile.circ as structural Verilog: 1 circuit, main circuit regfile
module regfile (
  input  [4:0] ReadIndex1,
  input  [4:0] ReadIndex2,
  input  [4:0] WriteIndex,
  input  [31:0] WriteData,
  input  RegWEn,
  input  clk,
  output [31:0] ra,
  output [31:0] sp,
  output [31:0] t0,
  output [31:0] t1,
  output [31:0] t2,
  output [31:0] s0,
  output [31:0] s1,
  output [31:0] a0,
  output [31:0] ReadData1,
  output [31:0] ReadData2
);

  wire demultiplexer_1_out1, demultiplexer_1_out2, demultiplexer_1_out3, demultiplexer_1_out4,
       demultiplexer_1_out5, demultiplexer_1_out6, demultiplexer_1_out7, demultiplexer_1_out8,
       demultiplexer_1_out9, demultiplexer_1_out10, demultiplexer_1_out11, demultiplexer_1_out12,
       demultiplexer_1_out13, demultiplexer_1_out14, demultiplexer_1_out15;
  wire [15:0] Dmux;
  wire [31:0] x0, x3, x4, x11, x12, x13, x14, x15, x16, x17, x18, x19, x20, x21, x22, x23, x24, x25, x26,
       x27, x28, x29, x30, x31;

  Register #(.width(32)) u_x0 (.D({32{1'b0}}), .en(1'b0), .clk(clk), .Q(x0));  // open: clr
  Register #(.width(32)) x1 (.D(WriteData), .en(demultiplexer_1_out1), .clk(clk), .Q(ra));  // open: clr
  Register #(.width(32)) x2 (.D(WriteData), .en(demultiplexer_1_out2), .clk(clk), .Q(sp));  // open: clr
  Register #(.width(32)) register_1 (.D(WriteData), .en(demultiplexer_1_out8), .clk(clk), .Q(s0));  // open: clr
  Demultiplexer #(.select(5)) demultiplexer_1 (
    .out1(demultiplexer_1_out1), .out2(demultiplexer_1_out2), .out3(demultiplexer_1_out3),
    .out4(demultiplexer_1_out4), .out5(demultiplexer_1_out5), .out6(demultiplexer_1_out6),
    .out7(demultiplexer_1_out7), .out8(demultiplexer_1_out8), .out9(demultiplexer_1_out9),
    .out10(demultiplexer_1_out10), .out11(demultiplexer_1_out11), .out12(demultiplexer_1_out12),
    .out13(demultiplexer_1_out13), .out14(demultiplexer_1_out14), .out15(demultiplexer_1_out15),
    .out16(Dmux[15]), .out17(Dmux[14]), .out18(Dmux[13]), .out19(Dmux[12]), .out20(Dmux[11]),
    .out21(Dmux[10]), .out22(Dmux[9]), .out23(Dmux[8]), .out24(Dmux[7]), .out25(Dmux[6]), .out26(Dmux[5]),
    .out27(Dmux[4]), .out28(Dmux[3]), .out29(Dmux[2]), .out30(Dmux[1]), .out31(Dmux[0]), .in(RegWEn),
    .sel(WriteIndex));  // open: out0
  Register #(.width(32)) u_x3 (.D(WriteData), .en(demultiplexer_1_out3), .clk(clk), .Q(x3));  // open: clr
  Register #(.width(32)) register_2 (.D(WriteData), .en(demultiplexer_1_out9), .clk(clk), .Q(s1));  // open: clr
  Register #(.width(32)) u_x4 (.D(WriteData), .en(demultiplexer_1_out4), .clk(clk), .Q(x4));  // open: clr
  Register #(.width(32)) register_3 (.D(WriteData), .en(demultiplexer_1_out10), .clk(clk), .Q(a0));  // open: clr
  Register #(.width(32)) x5 (.D(WriteData), .en(demultiplexer_1_out5), .clk(clk), .Q(t0));  // open: clr
  Register #(.width(32)) register_4 (.D(WriteData), .en(demultiplexer_1_out11), .clk(clk), .Q(x11));  // open: clr
  Register #(.width(32)) x6 (.D(WriteData), .en(demultiplexer_1_out6), .clk(clk), .Q(t1));  // open: clr
  Register #(.width(32)) register_5 (.D(WriteData), .en(demultiplexer_1_out12), .clk(clk), .Q(x12));  // open: clr
  Register #(.width(32)) x7 (.D(WriteData), .en(demultiplexer_1_out7), .clk(clk), .Q(t2));  // open: clr
  Register #(.width(32)) register_6 (.D(WriteData), .en(demultiplexer_1_out13), .clk(clk), .Q(x13));  // open: clr
  Register #(.width(32)) register_7 (.D(WriteData), .en(demultiplexer_1_out14), .clk(clk), .Q(x14));  // open: clr
  Register #(.width(32)) register_8 (.D(WriteData), .en(demultiplexer_1_out15), .clk(clk), .Q(x15));  // open: clr
  Multiplexer #(.select(5), .width(32)) multiplexer_1 (
    .in0(x0), .in1(ra), .in2(sp), .in3(x3), .in4(x4), .in5(t0), .in6(t1), .in7(t2), .in8(s0), .in9(s1),
    .in10(a0), .in11(x11), .in12(x12), .in13(x13), .in14(x14), .in15(x15), .in16(x16), .in17(x17),
    .in18(x18), .in19(x19), .in20(x20), .in21(x21), .in22(x22), .in23(x23), .in24(x24), .in25(x25),
    .in26(x26), .in27(x27), .in28(x28), .in29(x29), .in30(x30), .in31(x31), .out(ReadData2), .sel(ReadIndex2));
  Register #(.width(32)) register_9 (.D(WriteData), .en(Dmux[15]), .clk(clk), .Q(x16));  // open: clr
  Register #(.width(32)) register_10 (.D(WriteData), .en(Dmux[14]), .clk(clk), .Q(x17));  // open: clr
  Register #(.width(32)) register_11 (.D(WriteData), .en(Dmux[13]), .clk(clk), .Q(x18));  // open: clr
  Register #(.width(32)) register_12 (.D(WriteData), .en(Dmux[12]), .clk(clk), .Q(x19));  // open: clr
  Register #(.width(32)) register_13 (.D(WriteData), .en(Dmux[11]), .clk(clk), .Q(x20));  // open: clr
  Register #(.width(32)) register_14 (.D(WriteData), .en(Dmux[7]), .clk(clk), .Q(x24));  // open: clr
  Register #(.width(32)) register_15 (.D(WriteData), .en(Dmux[10]), .clk(clk), .Q(x21));  // open: clr
  Register #(.width(32)) register_16 (.D(WriteData), .en(Dmux[6]), .clk(clk), .Q(x25));  // open: clr
  Multiplexer #(.select(5), .width(32)) multiplexer_2 (
    .in0(x0), .in1(ra), .in2(sp), .in3(x3), .in4(x4), .in5(t0), .in6(t1), .in7(t2), .in8(s0), .in9(s1),
    .in10(a0), .in11(x11), .in12(x12), .in13(x13), .in14(x14), .in15(x15), .in16(x16), .in17(x17),
    .in18(x18), .in19(x19), .in20(x20), .in21(x21), .in22(x22), .in23(x23), .in24(x24), .in25(x25),
    .in26(x26), .in27(x27), .in28(x28), .in29(x29), .in30(x30), .in31(x31), .out(ReadData1), .sel(ReadIndex1));
  Register #(.width(32)) register_17 (.D(WriteData), .en(Dmux[9]), .clk(clk), .Q(x22));  // open: clr
  Register #(.width(32)) register_18 (.D(WriteData), .en(Dmux[5]), .clk(clk), .Q(x26));  // open: clr
  Register #(.width(32)) register_19 (.D(WriteData), .en(Dmux[8]), .clk(clk), .Q(x23));  // open: clr
  Register #(.width(32)) register_20 (.D(WriteData), .en(Dmux[4]), .clk(clk), .Q(x27));  // open: clr
  Register #(.width(32)) register_21 (.D(WriteData), .en(Dmux[3]), .clk(clk), .Q(x28));  // open: clr
  Register #(.width(32)) register_22 (.D(WriteData), .en(Dmux[2]), .clk(clk), .Q(x29));  // open: clr
  Register #(.width(32)) register_23 (.D(WriteData), .en(Dmux[1]), .clk(clk), .Q(x30));  // open: clr
  Register #(.width(32)) register_24 (.D(WriteData), .en(Dmux[0]), .clk(clk), .Q(x31));  // open: clr

  // Other names for the same wires on the sheet: x1[31:0] = ra; x2[31:0] = sp; x5[31:0] = t0; x6[31:0] = t1;
  //   x7[31:0] = t2; x8[31:0] = s0; x9[31:0] = s1; x10[31:0] = a0

  // Notes on the sheet:
  //   INPUTS to your circuit
  //   DON'T CHANGE THE LOCATIONS OF THE INPUTS AND OUTPUTS!
  //   These are DEBUG/TEST outputs from your circuit.
  //   OUTPUTS from your circuit
endmodule
